# Fritzing sketch battleship_16x16 (saved by Fritzing 0.9.3b)
breadboards: 4

parts:
  Part1 = Arduino Mega 2560 (Rev3)
  IC1 = Microchip MCP23008 8-bit I/O expander [part_number=MCP23008 package="DIP (Dual Inline) [THT]"]
  IC2 = Microchip MCP23008 8-bit I/O expander [part_number=MCP23008 package="DIP (Dual Inline) [THT]"]
  IC3 = Microchip MCP23008 8-bit I/O expander [part_number=MCP23008 package="DIP (Dual Inline) [THT]"]
  S1 = Pushbutton [package="[THT]"]
  S2 = Pushbutton [package="[THT]"]
  S3 = Pushbutton [package="[THT]"]
  S4 = Pushbutton [package="[THT]"]
  S5 = Pushbutton [package="[THT]"]
  S6 = Pushbutton [package="[THT]"]
  S7 = Pushbutton [package="[THT]"]
  S8 = Pushbutton [package="[THT]"]
  S9 = Pushbutton [package="[THT]"]
  S10 = Pushbutton [package="[THT]"]
  S11 = Pushbutton [package="[THT]"]
  S12 = Pushbutton [package="[THT]"]
  S13 = Pushbutton [package="[THT]"]
  S14 = Pushbutton [package="[THT]"]
  S15 = Pushbutton [package="[THT]"]
  S16 = Pushbutton [package="[THT]"]
  S17 = Pushbutton [package="[THT]"]
  S18 = Pushbutton [package="[THT]"]
  S19 = Pushbutton [package="[THT]"]
  S20 = Pushbutton [package="[THT]"]
  S21 = Pushbutton [package="[THT]"]
  S22 = Pushbutton [package="[THT]"]
  S23 = Pushbutton [package="[THT]"]
  S24 = Pushbutton [package="[THT]"]
  S25 = Pushbutton [package="[THT]"]
  YwRobot_Power_Supply1 = YwRobot Breadboard Power Supply [part_number=545043]

nets:
  N1: Part1.D21/SCL, IC1.SCL, IC2.SCL, IC3.SCL
  N2: Part1.D20/SDA, IC1.SDA, IC2.SDA, IC3.SDA
  N3: Part1.D9_PWM, S25.Pin_1, S25.Pin_2
  N4: Part1.GND, S1.Pin_3, S1.Pin_4, S2.Pin_3, S2.Pin_4, S3.Pin_3, S3.Pin_4, S4.Pin_3, S4.Pin_4, S5.Pin_3, S5.Pin_4, S6.Pin_3, S6.Pin_4, S7.Pin_3, S7.Pin_4, S8.Pin_3, S8.Pin_4, S9.Pin_3, S9.Pin_4, S10.Pin_3, S10.Pin_4, S11.Pin_3, S11.Pin_4, S12.Pin_3, S12.Pin_4, S25.Pin_3, S25.Pin_4, YwRobot_Power_Supply1.GND#13
  VSS: IC1.A2, IC1.A1, IC1.A0, IC1.VSS, IC2.A2, IC2.A1, IC2.VSS, IC3.A2, IC3.A0, IC3.VSS, S13.Pin_3, S13.Pin_4, S14.Pin_3, S14.Pin_4, S15.Pin_3, S15.Pin_4, S16.Pin_3, S16.Pin_4, S17.Pin_3, S17.Pin_4, S18.Pin_3, S18.Pin_4, S19.Pin_3, S19.Pin_4, S20.Pin_3, S20.Pin_4, S21.Pin_3, S21.Pin_4, S22.Pin_3, S22.Pin_4, S23.Pin_3, S23.Pin_4, S24.Pin_3, S24.Pin_4
  VDD: IC1.Reset, IC1.VDD, IC2.A0, IC2.Reset, IC2.VDD, IC3.A1, IC3.Reset, IC3.VDD
  N5: IC1.GP0, S17.Pin_1, S17.Pin_2
  N6: IC1.GP1, S18.Pin_1, S18.Pin_2
  N7: IC1.GP2, S19.Pin_1, S19.Pin_2
  N8: IC1.GP3, S20.Pin_1, S20.Pin_2
  N9: IC1.GP4, S21.Pin_1, S21.Pin_2
  N10: IC1.GP5, S22.Pin_1, S22.Pin_2
  N11: IC1.GP6, S23.Pin_1, S23.Pin_2
  N12: IC1.GP7, S24.Pin_1, S24.Pin_2
  N13: IC2.GP0, S4.Pin_1, S4.Pin_2
  N14: IC2.GP1, S3.Pin_1, S3.Pin_2
  N15: IC2.GP2, S2.Pin_1, S2.Pin_2
  N16: IC2.GP3, S1.Pin_1, S1.Pin_2
  N17: IC2.GP5, S14.Pin_1, S14.Pin_2
  N18: IC2.GP6, S15.Pin_1, S15.Pin_2
  N19: IC2.GP7, S16.Pin_1, S16.Pin_2
  N20: IC3.GP0, S12.Pin_1, S12.Pin_2
  N21: IC3.GP1, S11.Pin_1, S11.Pin_2
  N22: IC3.GP2, S10.Pin_1, S10.Pin_2
  N23: IC3.GP3, S9.Pin_1, S9.Pin_2
  N24: IC3.GP4, S8.Pin_1, S8.Pin_2
  N25: IC3.GP5, S7.Pin_1, S7.Pin_2
  N26: IC3.GP6, S6.Pin_1, S6.Pin_2
  N27: IC3.GP7, S5.Pin_1, S5.Pin_2
  N28: S13.Pin_1, S13.Pin_2

notes:
  16x16 matrix not shown. Red wire to red wire on matrix. Green wire to green wire on matrix. White wire to white wire on matrix.

custom parts:
  Microchip MCP23008 8-bit I/O expander: Provides 8-bit, general purpose, parallel I/O expansion for I2C bus. Datasheet: http://ww1.microchip.com/downloads/en/devicedoc/21919e.pdf
  YwRobot Breadboard Power Supply: The YwRobot Breadboard Power Supply (MB-V2) has two power rails; they can be 5V or 3V3. Power to the module can be provided through the female USB socket or through the A10 (female) 2.1mm power jack.
